// Logisim project s-mips.circ as structural Verilog
module S_MIPS_Board (
  input  DESHABILITAR_DISPATCHER,
  output halt
);

  wire button_1_out, CLK, CS, d_ff_1_q, LCLR, LoadRAM, LoadRAMOn, LW, R_R_W, R_W, ram_dispatcher_1_finished,
       RCS, Reset_out, RST, TTY_EN;
  wire [2:0] KDB;
  wire [3:0] LMask, Mask, ram_1_read_time, ram_1_write_time, RMask;
  wire [6:0] KDB_DATA, TTY_DATA;
  wire [15:0] Addr, LAddr, RAddr;
  wire [31:0] I0, I1, I2, I3, LData, ram_1_data_out_0, ram_1_data_out_1, ram_1_data_out_2, ram_1_data_out_3,
       RI0, RI1, RI2, RI3;

  TTY #(.rows(25), .cols(80)) tty_1 (.data(TTY_DATA), .clk(CLK), .we(TTY_EN), .clr(RST));
  not not_1 (LoadRAMOn, ram_dispatcher_1_finished);
  RAM_Dispatcher ram_dispatcher_1 (
    .WriteTime(ram_1_write_time), .Clock(CLK), .Data(LData), .Address(LAddr), .Mask(LMask),
    .Finished(ram_dispatcher_1_finished), .Write(LW), .CLR(LCLR));
  Keyboard #(.buflen(64)) keyboard_1 (.clk(CLK), .re(KDB[0]), .avail(KDB[2]), .data(KDB_DATA));  // open: clr
  RAM ram_1 (
    .Address(RAddr), .Data_Out_0(ram_1_data_out_0), .Data_Out_1(ram_1_data_out_1),
    .Data_Out_2(ram_1_data_out_2), .Data_Out_3(ram_1_data_out_3), .Data_In_0(RI0), .Data_In_1(RI1),
    .Data_In_2(RI2), .Data_In_3(RI3), .Mask(RMask), .nRead_Write(R_R_W), .Chip_Select(RCS),
    .Read_Time(ram_1_read_time), .Reset(button_1_out), .Write_Time(ram_1_write_time));
  Button button_1 (.out(button_1_out));
  D_Flip_Flop d_ff_1 (.clk(CLK), .D(1'b1), .Q(d_ff_1_q), .reset(Reset_out));  // open: Qn, preset, en
  Button Reset (.out(Reset_out));
  S_MIPS_2 s_mips_1 (
    .Kbd_Enable(KDB[0]), .Address(Addr), .Kbd_Clear(KDB[1]), .Kbd_Available(KDB[2]), .RAM_In_0(I0),
    .Kbd_ASCII_Data(KDB_DATA), .RAM_In_1(I1), .TTY_Enable(TTY_EN), .RAM_In_2(I2), .RAM_In_3(I3),
    .TTY_ASCII_Data(TTY_DATA), .Reset(RST), .RAM_Out_0(ram_1_data_out_0), .Clock(CLK),
    .RAM_Out_1(ram_1_data_out_1), .Stop(halt), .RAM_Out_2(ram_1_data_out_2), .RAM_Out_3(ram_1_data_out_3),
    .Mask(Mask), .Read_Time(ram_1_read_time), .Write_Time(ram_1_write_time), .nRead_Write(R_W),
    .Chip_Select(CS));
  D_Flip_Flop d_ff_2 (.clk(CLK), .D(d_ff_1_q), .Qn(LCLR), .reset(Reset_out));  // open: Q, preset, en
  or or_1 (RST, LCLR, LoadRAM);
  Clock clock_1 (.out(CLK));
  Multiplexer #(.width(32), .enable("false")) multiplexer_1 (.in0(I0), .in1(LData), .out(RI0), .sel(LoadRAM));
  Multiplexer #(.width(32), .enable("false")) multiplexer_2 (.in0(I1), .in1(LData), .out(RI1), .sel(LoadRAM));
  Multiplexer #(.width(32), .enable("false")) multiplexer_3 (.in0(I2), .in1(LData), .out(RI2), .sel(LoadRAM));
  Multiplexer #(.width(32), .enable("false")) multiplexer_4 (.in0(I3), .in1(LData), .out(RI3), .sel(LoadRAM));
  and and_1 (LoadRAM, ~DESHABILITAR_DISPATCHER, LoadRAMOn);  // AND_Gate
  Multiplexer #(.width(16), .enable("false")) multiplexer_5 (.in0(Addr), .in1(LAddr), .out(RAddr), .sel(LoadRAM));
  Multiplexer #(.width(4), .enable("false")) multiplexer_6 (.in0(Mask), .in1(LMask), .out(RMask), .sel(LoadRAM));
  Multiplexer #(.enable("false")) multiplexer_7 (.in0(CS), .in1(LW), .out(RCS), .sel(LoadRAM));
  Multiplexer #(.enable("false")) multiplexer_8 (.in0(R_W), .in1(LW), .out(R_R_W), .sel(LoadRAM));

  // Notes on the sheet:
  //   NO MODIFICAR
  //   Keyboard
endmodule

module RAM (
  input  [15:0] Address,
  input  [31:0] Data_In_0,
  input  [31:0] Data_In_1,
  input  [31:0] Data_In_2,
  input  [31:0] Data_In_3,
  input  [3:0] Mask,
  input  nRead_Write,
  input  Chip_Select,
  input  Reset,
  output [31:0] Data_Out_0,
  output [31:0] Data_Out_1,
  output [31:0] Data_Out_2,
  output [31:0] Data_Out_3,
  output [3:0] Read_Time,
  output [3:0] Write_Time
);

  wire and_2_out, and_3_out, and_4_out, and_5_out, and_6_out, and_7_out, and_8_out, and_9_out, Changed, CLK,
       comparator_2_eq, comparator_3_eq, comparator_4_eq, comparator_5_eq, comparator_6_eq, Count,
       demultiplexer_3_out0, Idle, Idle_q, Load, Load0, Load1, nand_1_out, or_1_out, or_2_out, or_3_out,
       or_4_out, or_5_out, or_6_out, or_7_out, or_8_out, or_9_out, or_10_out, Proc_q, Update_Mem, Zero_Time;
  wire [3:0] counter_1_q, multiplexer_1_out, subtractor_1_out;
  wire [31:0] register_1_q, register_2_q, register_3_q, register_4_q, register_5_q;

  // Probe on 4'b0011
  // Probe on 4'b0010
  Multiplexer #(.width(4), .enable("false")) multiplexer_1 (
    .in0(4'b0011), .in1(4'b0010), .out(multiplexer_1_out), .sel(nRead_Write));
  or or_1 (or_1_out, Idle, Update_Mem);
  or or_2 (or_2_out, ~Chip_Select, Reset);  // OR_Gate
  Subtractor #(.width(4)) subtractor_1 (.a(multiplexer_1_out), .b(4'b0010), .out(subtractor_1_out));  // open: bin, bout
  Demultiplexer #(.enable("false")) demultiplexer_1 (.out0(Idle), .out1(Load0), .in(Idle_q), .sel(Changed));
  D_Flip_Flop u_Idle (.clk(CLK), .D(or_1_out), .Q(Idle_q), .preset(or_2_out));  // open: Qn, en, reset
  // Probe on counter_1_q
  Counter #(.width(4), .max('hf)) counter_1 (
    .load(Load), .D(subtractor_1_out), .count(Count), .Q(counter_1_q), .clk(CLK), .clr(or_3_out));  // open: carry
  or or_3 (or_3_out, ~Chip_Select, Reset);  // OR_Gate
  Comparator #(.width(4), .mode("unsigned")) comparator_1 (
    .a(4'b0000), .b(counter_1_q), .eq(Zero_Time));  // open: gt, lt
  or or_4 (or_4_out, Count, Load0, Load1);
  Register #(.width(32)) register_1 (.D(Data_In_0), .en(Chip_Select), .Q(register_1_q), .clk(CLK), .clr(or_5_out));
  or or_5 (or_5_out, ~Chip_Select, Reset);  // OR_Gate
  Register #(.width(32)) register_2 (.D(Data_In_1), .en(Chip_Select), .Q(register_2_q), .clk(CLK), .clr(or_6_out));
  or or_6 (or_6_out, ~Chip_Select, Reset);  // OR_Gate
  Register #(.width(32)) register_3 (.D(Data_In_2), .en(Chip_Select), .Q(register_3_q), .clk(CLK), .clr(or_7_out));
  or or_7 (or_7_out, ~Chip_Select, Reset);  // OR_Gate
  Register #(.width(32)) register_4 (.D(Data_In_3), .en(Chip_Select), .Q(register_4_q), .clk(CLK), .clr(or_8_out));
  or or_8 (or_8_out, ~Chip_Select, Reset);  // OR_Gate
  Register #(.width(32)) register_5 (
    .D({{11{1'b1}}, nRead_Write, Mask, Address}), .en(Chip_Select), .Q(register_5_q), .clk(CLK),
    .clr(or_9_out));
  or or_9 (or_9_out, ~Chip_Select, Reset);  // OR_Gate
  D_Flip_Flop Proc (.clk(CLK), .D(or_4_out), .Q(Proc_q), .reset(or_10_out));  // open: Qn, preset, en
  or or_10 (or_10_out, ~Chip_Select, Reset);  // OR_Gate
  Demultiplexer #(.enable("false")) demultiplexer_2 (
    .out0(Count), .out1(Update_Mem), .in(demultiplexer_3_out0), .sel(Zero_Time));
  Demultiplexer #(.enable("false")) demultiplexer_3 (
    .out0(demultiplexer_3_out0), .out1(Load1), .in(Proc_q), .sel(Changed));
  Clock clock_1 (.out(CLK));
  Comparator #(.width(32)) comparator_2 (.a(register_1_q), .b(Data_In_0), .eq(comparator_2_eq));  // open: gt, lt
  Comparator #(.width(32)) comparator_3 (.a(register_2_q), .b(Data_In_1), .eq(comparator_3_eq));  // open: gt, lt
  Comparator #(.width(32)) comparator_4 (.a(register_3_q), .b(Data_In_2), .eq(comparator_4_eq));  // open: gt, lt
  Comparator #(.width(32)) comparator_5 (.a(register_4_q), .b(Data_In_3), .eq(comparator_5_eq));  // open: gt, lt
  Comparator #(.width(32)) comparator_6 (
    .a(register_5_q), .b({{11{1'b1}}, nRead_Write, Mask, Address}), .eq(comparator_6_eq));  // open: gt, lt
  nand nand_1 (nand_1_out, comparator_6_eq, comparator_2_eq, comparator_3_eq, comparator_4_eq, comparator_5_eq);
  and and_1 (Changed, nand_1_out, Chip_Select);
  or or_11 (Load, Count, Load1, Load0);
  and and_2 (and_2_out, Mask[0], Update_Mem, nRead_Write);
  and and_3 (and_3_out, Mask[1], Update_Mem, nRead_Write);
  and and_4 (and_4_out, Mask[2], Update_Mem, nRead_Write);
  and and_5 (and_5_out, Mask[3], Update_Mem, nRead_Write);
  RAM_part #(.addrWidth(16), .dataWidth(32), .bus("separate")) ram_1 (
    .addr(Address), .din(Data_In_0), .data(Data_Out_0), .str(and_2_out), .sel(Chip_Select), .clk(CLK),
    .ld(and_6_out), .clr(Reset));
  and and_6 (and_6_out, ~nRead_Write, Idle);  // AND_Gate
  RAM_part #(.addrWidth(16), .dataWidth(32), .bus("separate")) ram_2 (
    .addr(Address), .din(Data_In_1), .data(Data_Out_1), .str(and_3_out), .sel(Chip_Select), .clk(CLK),
    .ld(and_7_out), .clr(Reset));
  and and_7 (and_7_out, ~nRead_Write, Idle);  // AND_Gate
  RAM_part #(.addrWidth(16), .dataWidth(32), .bus("separate")) ram_3 (
    .addr(Address), .din(Data_In_2), .data(Data_Out_2), .str(and_4_out), .sel(Chip_Select), .clk(CLK),
    .ld(and_8_out), .clr(Reset));
  and and_8 (and_8_out, ~nRead_Write, Idle);  // AND_Gate
  RAM_part #(.addrWidth(16), .dataWidth(32), .bus("separate")) ram_4 (
    .addr(Address), .din(Data_In_3), .data(Data_Out_3), .str(and_5_out), .sel(Chip_Select), .clk(CLK),
    .ld(and_9_out), .clr(Reset));
  and and_9 (and_9_out, ~nRead_Write, Idle);  // AND_Gate

  assign Read_Time = 4'b0011;
  assign Write_Time = 4'b0010;

  // Other names for the same wires on the sheet: M0 = Mask[0]; M1 = Mask[1]; M2 = Mask[2]; M3 = Mask[3];
  //   RW = nRead_Write; CLR = Reset; CS = Chip_Select; Load2 = Count

  // Notes on the sheet:
  //   NO MODIFICAR
  //   excepto quizás los valores RT y WT
  //   BANK0
  //   BANK1
  //   BANK2
  //   BANK3
endmodule

module RAM_Dispatcher (
  input  [3:0] WriteTime,
  input  Clock,
  input  CLR,
  output [31:0] Data,
  output [15:0] Address,
  output [3:0] Mask,
  output Finished,
  output Write
);

  wire demultiplexer_2_out1, demultiplexer_3_out1, End, IDLE_q, IncAddr, Load, or_1_out, or_2_out, While_q,
       WriteEnd;
  wire [3:0] counter_1_q;
  wire [31:0] CurrentAddress_q;

  Counter #(.width(32), .max('hffffffff)) CurrentAddress (
    .count(IncAddr), .Q({CurrentAddress_q[31:18], Address, CurrentAddress_q[1:0]}), .clk(Clock), .clr(CLR));  // open: load, D, carry
  or or_1 (or_1_out, IncAddr, demultiplexer_3_out1, Finished);
  D_Flip_Flop IDLE (.clk(Clock), .D(or_1_out), .Q(IDLE_q), .preset(CLR));  // open: Qn, en, reset
  Demultiplexer #(.enable("false")) demultiplexer_1 (.out0(Load), .out1(Finished), .in(IDLE_q), .sel(End));
  D_Flip_Flop While (.clk(Clock), .D(or_2_out), .Q(While_q), .reset(CLR));  // open: Qn, preset, en
  or or_2 (or_2_out, Write, Load);
  RAM_part #(.addrWidth(18), .dataWidth(32)) ram_1 (
    .addr({Address, CurrentAddress_q[1:0]}), .data(Data), .clk(Clock));  // open: sel, ld, clr
  Demultiplexer #(.enable("false")) demultiplexer_2 (
    .out0(Write), .out1(demultiplexer_2_out1), .in(While_q), .sel(WriteEnd));
  Decoder #(.select(2)) decoder_1 (
    .out0(Mask[0]), .out1(Mask[1]), .out2(Mask[2]), .out3(Mask[3]), .sel(CurrentAddress_q[1:0]));  // open: en
  Demultiplexer #(.enable("false")) demultiplexer_3 (
    .out0(IncAddr), .out1(demultiplexer_3_out1), .in(demultiplexer_2_out1), .sel(End));
  Counter #(.width(4), .max('hf)) counter_1 (
    .load(Load), .D(WriteTime), .count(Write), .Q(counter_1_q), .clk(Clock));  // open: carry, clr
  Comparator #(.width(32)) comparator_1 (.a(Data), .b({32{1'b1}}), .eq(End));  // open: gt, lt
  Comparator #(.width(4)) comparator_2 (.a(4'b0000), .b(counter_1_q), .eq(WriteEnd));  // open: gt, lt

  // Other names for the same wires on the sheet: CLK = Clock; Count = Write; WT[3:0] = WriteTime
endmodule

module S_MIPS_2 (
  input  Kbd_Available,
  input  [6:0] Kbd_ASCII_Data,
  input  [31:0] RAM_Out_0,
  input  [31:0] RAM_Out_1,
  input  Reset,
  input  [31:0] RAM_Out_2,
  input  Clock,
  input  [31:0] RAM_Out_3,
  input  [3:0] Read_Time,
  input  [3:0] Write_Time,
  output Kbd_Enable,
  output [15:0] Address,
  output Kbd_Clear,
  output TTY_Enable,
  output [6:0] TTY_ASCII_Data,
  output Stop,
  output [31:0] RAM_In_0,
  output [31:0] RAM_In_1,
  output [31:0] RAM_In_2,
  output [31:0] RAM_In_3,
  output [3:0] Mask,
  output nRead_Write,
  output Chip_Select
);

  wire d_ff_1_q, Get_Data, Get_Inst, Inst_EN, PC_EN, Ready_Data, Ready_Inst, Ready_Write, Reg_EN, SP_EN,
       START, START_EN, Write_Data;
  wire [5:0] F_Code, Op_Code;
  wire [31:0] bit_extender_1_out, DP_Address, Inst, multiplexer_1_out;

  Multiplexer #(.width(32)) multiplexer_1 (
    .in0({32{1'b1}}), .in1(bit_extender_1_out), .out(multiplexer_1_out), .sel(Kbd_Available));  // open: en
  assign bit_extender_1_out = {{25{1'b0}}, Kbd_ASCII_Data};  // Bit_Extender bit_extender_1
  D_Flip_Flop #(.trigger("falling")) d_ff_1 (
    .clk(Clock), .D(1'b0), .Q(d_ff_1_q), .preset(Reset));  // open: Qn, en, reset
  Data_Path data_path_1 (
    .Instruccion(Inst), .KBD(multiplexer_1_out), .CLK(Clock), .Res(Reset), .ID_EN(Inst_EN), .PC_EN(PC_EN),
    .R_W(Reg_EN), .Start(START_EN), .KBD_EN(Kbd_Enable), .SPEN(SP_EN), .MemoryAddres(DP_Address),
    .Data_Ram(RAM_In_0), .TTY(TTY_ASCII_Data), .Op_Code(Op_Code), .F_Code(F_Code));
  D_Flip_Flop #(.trigger("falling")) d_ff_2 (
    .clk(Clock), .D(d_ff_1_q), .Q(START), .reset(Reset));  // open: Qn, preset, en
  Control_Unit control_unit_1 (
    .in_1(START), .in_2(Clock), .in_3(Reset), .in_4(Ready_Inst), .in_5(Ready_Data), .in_6(Ready_Write),
    .in_7(Op_Code), .in_8(F_Code), .Get_Inst(Get_Inst), .PCen(PC_EN), .SPen(SP_EN), .INSTen(Inst_EN),
    .KBDen(Kbd_Enable), .RegW(Reg_EN), .TTYen(TTY_Enable), .WriteD(Write_Data), .startEN(START_EN),
    .Get_Data(Get_Data), .End(Stop));
  Access access_1 (
    .Address(DP_Address), .Ram_00(RAM_Out_0), .Ram_01(RAM_Out_1), .Ram_10(RAM_Out_2), .Ram_11(RAM_Out_3),
    .Read_Time(Read_Time), .Write_Time(Write_Time), .Read(Write_Data), .CLK(Clock), .RES(Reset),
    .Read_Inst(Get_Inst), .Read_Data(Get_Data), .Load(Inst_EN), .Mask(Mask), .RAM_OUT(Inst),
    .RW(nRead_Write), .Chip_Select(Chip_Select), .Ready_Inst(Ready_Inst), .Ready_Data(Ready_Data),
    .Ready_write(Ready_Write), .Address_2(Address));

  assign Kbd_Clear = Reset;
  assign RAM_In_1 = RAM_In_0;
  assign RAM_In_2 = RAM_In_0;
  assign RAM_In_3 = RAM_In_0;

  // Other names for the same wires on the sheet: CLK = Clock; CS = Chip_Select; KBD_AVAIL = Kbd_Available;
  //   CLR = Reset; KBD_CLR = Reset; KBD_DATA[6:0] = Kbd_ASCII_Data; RAM_A[15:0] = Address; DATA_RAM[31:0] = RAM_In_0;
  //   RAM_INPUT_0[31:0] = RAM_In_0; RAM_INPUT_1[31:0] = RAM_In_0; RAM_INPUT_2[31:0] = RAM_In_0;
  //   RAM_INPUT_3[31:0] = RAM_In_0; RAM_MASK[3:0] = Mask; RAM_OUTPUT_0[31:0] = RAM_Out_0;
  //   RAM_OUTPUT_1[31:0] = RAM_Out_1; RAM_OUTPUT_2[31:0] = RAM_Out_2; RAM_OUTPUT_3[31:0] = RAM_Out_3;
  //   RW = nRead_Write; TTY_DATA[6:0] = TTY_ASCII_Data

  // Notes on the sheet:
  //   RAM ADDRESS
  //   DATA FROM RAM
  //   DATA TO RAM
  //   DATA WRITE MASK
  //   RAM TIMING
  //   RAM CONTROL
  //   KEYBOARD
  //   TTY
  //   SEQUENCING
endmodule

module ALU_2 (
  input  [31:0] in_1,
  input  [31:0] in_2,
  input  [5:0] Func_Code,
  input  [5:0] Op_Code,
  input  [15:0] Constante,
  input  Tipo_de_Instruccion,
  output [31:0] Output,
  output [31:0] Hi,
  output [31:0] LO,
  output L_HI_LO
);

  wire tunnel;
  wire [3:0] Op;
  wire [31:0] B_Constante, multiplexer_1_out;

  Multiplexer #(.width(32)) multiplexer_1 (
    .in0(in_2), .in1(B_Constante), .out(multiplexer_1_out), .sel(Tipo_de_Instruccion));  // open: en
  ALU_Control alu_control_1 (
    .Func_Code(Func_Code), .Op_Code(Op_Code), .Constante(Constante), .Output(B_Constante), .Selector(Op),
    .L_HI_LO(L_HI_LO), .out_4(tunnel));
  ALU_Operations alu_operations_1 (
    .in_3(tunnel), .in_1(in_1), .in_2(multiplexer_1_out), .Output(Output), .in_4(Op), .Hi(Hi), .LO(LO));

  // Other names for the same wires on the sheet: A[31:0] = in_1; B[31:0] = in_2; Type_I = Tipo_de_Instruccion
endmodule

module ALU_Operations (
  input  [31:0] in_1,
  input  [31:0] in_2,
  input  in_3,
  input  [3:0] in_4,
  output [31:0] Output,
  output [31:0] Hi,
  output [31:0] LO
);

  wire Sel_Mul;
  wire [31:0] add, \and , Mul_HI, Mul_LO, \nor , \or , Remander, Result, slt_sltu, Sub, \xor ;

  Adder #(.width(32)) adder_1 (.a(in_1), .b(in_2), .out(add));  // open: cin, cout
  Subtractor #(.width(32)) subtractor_1 (.a(in_1), .b(in_2), .out(Sub));  // open: bin, bout
  Multi multi_1 (.in_1(in_1), .in_2(in_2), .HI(Mul_HI), .LO(Mul_LO), .in_3(in_3));
  Divi divi_1 (.out_4(Result), .out_5(Remander), .in_1(in_1), .in_2(in_2), .in_3(in_3));
  assign \and  = in_1 & in_2;  // AND_Gate and_1, 32 bits wide
  assign \or  = in_1 | in_2;  // OR_Gate or_1, 32 bits wide
  assign \xor  = in_1 ^ in_2;  // XOR_Gate xor_1, 32 bits wide
  assign \nor  = ~(in_1 | in_2);  // NOR_Gate nor_1, 32 bits wide
  Comparer comparer_1 (.in_1(in_1), .in_2(in_2), .Output(slt_sltu), .in_3(in_3));
  Comparator #(.width(4)) comparator_1 (.a(in_4), .b(4'b0010), .eq(Sel_Mul));  // open: gt, lt
  Multiplexer #(.select(4), .width(32)) multiplexer_1 (
    .in0(add), .in1(Sub), .in4(\and ), .in5(\or ), .in6(\nor ), .in7(\xor ), .in8(slt_sltu), .out(Output),
    .sel(in_4));  // open: in2, in3, in9, in10, in11, in12, in13, in14, in15, en
  Multiplexer #(.width(32)) multiplexer_2 (.in0(Remander), .in1(Mul_HI), .out(Hi), .sel(Sel_Mul));  // open: en
  Multiplexer #(.width(32)) multiplexer_3 (.in0(Result), .in1(Mul_LO), .out(LO), .sel(Sel_Mul));  // open: en

  // Other names for the same wires on the sheet: A[31:0] = in_1; B[31:0] = in_2; Op[3:0] = in_4; tunnel = in_3

  // Notes on the sheet:
  //   Arithmetics
  //   Logic
  //   COMPARER
endmodule

module ALU_Control (
  input  [5:0] Func_Code,
  input  [5:0] Op_Code,
  input  [15:0] Constante,
  output out_4,
  output L_HI_LO,
  output [31:0] Output,
  output [3:0] Selector
);

  wire add, addi, \and , and_13_out, andi, comparator_1_eq, comparator_2_eq, comparator_3_eq,
       comparator_4_eq, comparator_5_eq, comparator_6_eq, comparator_7_eq, comparator_8_eq, comparator_9_eq,
       comparator_10_eq, comparator_11_eq, comparator_12_eq, comparator_13_eq, div, divu, mult, mulu, \nor ,
       \or , ori, slt, slti, sltiu, sltu, sub, \xor , xori;

  Comparator #(.width(6)) comparator_1 (.a(Op_Code), .b({6{1'b0}}), .eq(comparator_1_eq));  // open: gt, lt
  Comparator #(.width(6)) comparator_2 (.a(Func_Code), .b(6'b100000), .eq(comparator_2_eq));  // open: gt, lt
  Comparator #(.width(6)) comparator_3 (.a(Func_Code), .b(6'b100010), .eq(comparator_3_eq));  // open: gt, lt
  Comparator #(.width(6)) comparator_4 (.a(Func_Code), .b(6'b011000), .eq(comparator_4_eq));  // open: gt, lt
  Comparator #(.width(6)) comparator_5 (.a(Func_Code), .b(6'b011001), .eq(comparator_5_eq));  // open: gt, lt
  Comparator #(.width(6)) comparator_6 (.a(Func_Code), .b(6'b011010), .eq(comparator_6_eq));  // open: gt, lt
  Comparator #(.width(6)) comparator_7 (.a(Func_Code), .b(6'b011011), .eq(comparator_7_eq));  // open: gt, lt
  Comparator #(.width(6)) comparator_8 (.a(Func_Code), .b(6'b100100), .eq(comparator_8_eq));  // open: gt, lt
  Comparator #(.width(6)) comparator_9 (.a(Func_Code), .b(6'b100101), .eq(comparator_9_eq));  // open: gt, lt
  Comparator #(.width(6)) comparator_10 (.a(Func_Code), .b(6'b100111), .eq(comparator_10_eq));  // open: gt, lt
  Comparator #(.width(6)) comparator_11 (.a(Func_Code), .b(6'b101000), .eq(comparator_11_eq));  // open: gt, lt
  Comparator #(.width(6)) comparator_12 (.a(Func_Code), .b(6'b101010), .eq(comparator_12_eq));  // open: gt, lt
  Comparator #(.width(6)) comparator_13 (.a(Func_Code), .b(6'b101011), .eq(comparator_13_eq));  // open: gt, lt
  and and_1 (add, comparator_1_eq, comparator_2_eq);
  and and_2 (sub, comparator_1_eq, comparator_3_eq);
  and and_3 (mult, comparator_1_eq, comparator_4_eq);
  and and_4 (mulu, comparator_1_eq, comparator_5_eq);
  and and_5 (div, comparator_1_eq, comparator_6_eq);
  and and_6 (divu, comparator_1_eq, comparator_7_eq);
  and and_7 (\and , comparator_1_eq, comparator_8_eq);
  and and_8 (\or , comparator_1_eq, comparator_9_eq);
  and and_9 (\nor , comparator_1_eq, comparator_10_eq);
  and and_10 (\xor , comparator_1_eq, comparator_11_eq);
  and and_11 (slt, comparator_1_eq, comparator_12_eq);
  and and_12 (sltu, comparator_1_eq, comparator_13_eq);
  Comparator #(.width(6)) comparator_14 (.a(Op_Code), .b(6'b001000), .eq(addi));  // open: gt, lt
  Comparator #(.width(6)) comparator_15 (.a(Op_Code), .b(6'b001100), .eq(andi));  // open: gt, lt
  Comparator #(.width(6)) comparator_16 (.a(Op_Code), .b(6'b001101), .eq(ori));  // open: gt, lt
  Comparator #(.width(6)) comparator_17 (.a(Op_Code), .b(6'b001110), .eq(xori));  // open: gt, lt
  Comparator #(.width(6)) comparator_18 (.a(Op_Code), .b(6'b001010), .eq(slti));  // open: gt, lt
  Comparator #(.width(6)) comparator_19 (.a(Op_Code), .b(6'b001011), .eq(sltiu));  // open: gt, lt
  or or_1 (Selector[0], sub, div, divu, \xor , \or , ori, xori);
  or or_2 (Selector[1], mult, mulu, div, \xor , divu, \nor , xori);
  or or_3 (Selector[2], \and , andi, \or , \xor , ori, \nor , xori);
  or or_4 (Selector[3], slt, sltu, slti, sltiu);
  or or_5 (out_4, mult, div, slt, slti);
  or or_6 (L_HI_LO, mult, div, mulu, divu);
  and and_13 (and_13_out, Constante[15], ~andi, ~ori, ~xori);  // AND_Gate
  assign Output[31:15] = {{16{and_13_out}}, and_13_out};  // Bit_Extender bit_extender_1

  assign Output[14:0] = Constante[14:0];
endmodule

module Multi (
  input  [31:0] in_1,
  input  [31:0] in_2,
  input  in_3,
  output [31:0] HI,
  output [31:0] LO
);

  wire SignA, SignB;
  wire [31:0] Hi_t, Lo_t, multiplexer_1_out, multiplexer_2_out, negator_1_out, negator_2_out, UnSignedHi,
       UnSignedLo;

  Negator #(.width(32)) negator_1 (.in(in_1), .out(negator_1_out));
  Negator #(.width(32)) negator_2 (.in(in_2), .out(negator_2_out));
  and and_1 (SignA, in_1[31], in_3);
  Multiplexer #(.width(32)) multiplexer_1 (
    .in0(in_1), .in1(negator_1_out), .out(multiplexer_1_out), .sel(SignA));  // open: en
  Multiplexer #(.width(32)) multiplexer_2 (
    .in0(in_2), .in1(negator_2_out), .out(multiplexer_2_out), .sel(SignB));  // open: en
  Multiplier #(.width(32)) multiplier_1 (
    .a(multiplexer_1_out), .b(multiplexer_2_out), .out(UnSignedLo), .cout(UnSignedHi));  // open: cin
  and and_2 (SignB, in_2[31], in_3);
  Multiplier #(.width(32)) multiplier_2 (.a(in_1), .b(in_2), .out(Lo_t), .cout(Hi_t));  // open: cin
  Multiplexer #(.width(32)) multiplexer_3 (.in0(UnSignedHi), .in1(Hi_t), .out(HI), .sel(in_3));  // open: en
  Multiplexer #(.width(32)) multiplexer_4 (.in0(UnSignedLo), .in1(Lo_t), .out(LO), .sel(in_3));  // open: en

  // Other names for the same wires on the sheet: A[31:0] = in_1; B[31:0] = in_2; Sign = in_3
endmodule

module Divi (
  input  [31:0] in_1,
  input  [31:0] in_2,
  input  in_3,
  output [31:0] out_4,
  output [31:0] out_5
);

  wire SignA, SignB, SignResult;
  wire [31:0] A_t, adder_1_out, B_t, divider_1_out, multiplexer_4_out, negator_1_out, negator_2_out,
       negator_3_out, rem, subtractor_1_out;

  Negator #(.width(32)) negator_1 (.in(in_2), .out(negator_1_out));
  and and_1 (SignA, in_1[31], in_3);
  Multiplexer #(.width(32)) multiplexer_1 (.in0(in_1), .in1(negator_2_out), .out(A_t), .sel(SignA));  // open: en
  Negator #(.width(32)) negator_2 (.in(in_1), .out(negator_2_out));
  Multiplexer #(.width(32)) multiplexer_2 (.in0(in_2), .in1(negator_1_out), .out(B_t), .sel(SignB));  // open: en
  and and_2 (SignB, in_2[31], in_3);
  Divider #(.width(32)) divider_1 (.a(A_t), .b(B_t), .out(divider_1_out), .rem(rem));  // open: upper
  xor xor_1 (SignResult, SignA, SignB);
  Subtractor #(.width(32)) subtractor_1 (.a(B_t), .b(rem), .out(subtractor_1_out));  // open: bin, bout
  Adder #(.width(32)) adder_1 (.a(divider_1_out), .b(32'h1), .out(adder_1_out));  // open: cin, cout
  Multiplexer #(.width(32)) multiplexer_3 (.in0(rem), .in1(subtractor_1_out), .out(out_5), .sel(SignA));  // open: en
  Multiplexer #(.width(32)) multiplexer_4 (
    .in0(divider_1_out), .in1(adder_1_out), .out(multiplexer_4_out), .sel(SignA));  // open: en
  Negator #(.width(32)) negator_3 (.in(multiplexer_4_out), .out(negator_3_out));
  Multiplexer #(.width(32)) multiplexer_5 (
    .in0(multiplexer_4_out), .in1(negator_3_out), .out(out_4), .sel(SignResult));  // open: en

  // Other names for the same wires on the sheet: A[31:0] = in_1; B[31:0] = in_2; remainder[31:0] = out_5;
  //   Result[31:0] = out_4; Sign = in_3
endmodule

module Comparer (
  input  [31:0] in_1,
  input  [31:0] in_2,
  input  in_3,
  output [31:0] Output
);

  wire multiplexer_1_out, slt, sltu;

  Comparator #(.width(32)) comparator_1 (.a(in_1), .b(in_2), .lt(slt));  // open: gt, eq
  Comparator #(.width(32), .mode("unsigned")) comparator_2 (.a(in_1), .b(in_2), .lt(sltu));  // open: gt, eq
  Multiplexer multiplexer_1 (.in0(sltu), .in1(slt), .out(multiplexer_1_out), .sel(in_3));  // open: en
  assign Output = {{31{1'b0}}, multiplexer_1_out};  // Bit_Extender bit_extender_1

  // Other names for the same wires on the sheet: A[31:0] = in_1; B[31:0] = in_2; Out[31:0] = Output; Sign = in_3
endmodule

module Register_File (
  input  [31:0] in_1,
  input  [31:0] in_2,
  input  [31:0] in_3,
  input  [4:0] in_4,
  input  [4:0] in_5,
  input  [4:0] in_6,
  input  in_7,
  input  in_8,
  input  in_9,
  input  SPEN,
  input  in_11,
  input  in_12,
  input  in_13,
  input  in_14,
  input  in_15,
  input  in_16,
  output [31:0] Output,
  output [31:0] out_18,
  output [31:0] out_19,
  output [31:0] out_20,
  output [31:0] out_21
);

  wire and_1_out, L0, L1, L2, L3, L4, L5, L6, L7, L8, L9, L10, L11, L12, L13, L14, L15, L16, L17, L18, L19,
       L20, L21, L22, L23, L24, L25, L26, L27, L28, L29, L30, L31, LSP, or_1_out;
  wire [1:0] Selector;
  wire [31:0] adder_1_out, Input, multiplexer_2_out, multiplexer_6_out, Q0, Q1, Q2, Q3, Q4, Q5, Q6, Q7, Q8,
       Q9, Q10, Q11, Q12, Q13, Q14, Q15, Q16, Q17, Q18, Q19, Q20, Q21, Q22, Q23, Q24, Q25, Q26, Q27, Q28,
       Q29, Q30, Random, SP;

  Register #(.width(32)) register_1 (.D({32{1'b0}}), .en(L0), .Q(Q0), .clk(in_9), .clr(in_8));
  Register #(.width(32)) register_2 (.D(Input), .en(L8), .Q(Q8), .clk(in_9), .clr(in_8));
  Register #(.width(32)) register_3 (.D(Input), .en(L16), .Q(Q16), .clk(in_9), .clr(in_8));
  Register #(.width(32)) register_4 (.D(Input), .en(L24), .Q(Q24), .clk(in_9), .clr(in_8));
  Register #(.width(32)) register_5 (.D(in_2), .en(in_11), .Q(out_20), .clk(in_9), .clr(in_8));
  Register #(.width(32)) register_6 (.D(Input), .en(L1), .Q(Q1), .clk(in_9), .clr(in_8));
  Register #(.width(32)) register_7 (.D(Input), .en(L9), .Q(Q9), .clk(in_9), .clr(in_8));
  Register #(.width(32)) register_8 (.D(Input), .en(L17), .Q(Q17), .clk(in_9), .clr(in_8));
  Register #(.width(32)) register_9 (.D(Input), .en(L25), .Q(Q25), .clk(in_9), .clr(in_8));
  Register #(.width(32)) register_10 (.D(in_3), .en(in_11), .Q(out_18), .clk(in_9), .clr(in_8));
  Register #(.width(32)) register_11 (.D(Input), .en(L2), .Q(Q2), .clk(in_9), .clr(in_8));
  Register #(.width(32)) register_12 (.D(Input), .en(L10), .Q(Q10), .clk(in_9), .clr(in_8));
  Register #(.width(32)) register_13 (.D(Input), .en(L18), .Q(Q18), .clk(in_9), .clr(in_8));
  Register #(.width(32)) register_14 (.D(Input), .en(L26), .Q(Q26), .clk(in_9), .clr(in_8));
  Multiplexer #(.select(2), .width(32)) multiplexer_1 (
    .in0(in_1), .in1(out_20), .in2(out_18), .in3(Random), .out(Input), .sel(Selector));  // open: en
  Multiplexer #(.width(32)) multiplexer_2 (
    .in0(32'h4), .in1(32'hfffffffc), .out(multiplexer_2_out), .sel(in_13));  // open: en
  or or_1 (or_1_out, in_13, in_15);
  Random #(.width(32), .seed(7)) random_1 (.clk(in_9), .out(Random));  // open: next, clr
  Adder #(.width(32)) adder_1 (.a(multiplexer_2_out), .b(out_21), .out(adder_1_out));  // open: cin, cout
  and and_1 (and_1_out, or_1_out, SPEN);
  Register #(.width(32)) register_15 (.D(Input), .en(L3), .Q(Q3), .clk(in_9), .clr(in_8));
  Register #(.width(32)) register_16 (.D(Input), .en(L11), .Q(Q11), .clk(in_9), .clr(in_8));
  Register #(.width(32)) register_17 (.D(Input), .en(L19), .Q(Q19), .clk(in_9), .clr(in_8));
  Register #(.width(32)) register_18 (.D(Input), .en(L27), .Q(Q27), .clk(in_9), .clr(in_8));
  or or_2 (Selector[0], in_12, in_14);
  or or_3 (Selector[1], in_16, in_12);
  Multiplexer #(.width(32)) multiplexer_3 (.in0(adder_1_out), .in1({32{1'b1}}), .out(SP), .sel(in_8));  // open: en
  or or_4 (LSP, and_1_out, L31, in_8);
  Register #(.width(32)) register_19 (.D(Input), .en(L4), .Q(Q4), .clk(in_9), .clr(in_8));
  Register #(.width(32)) register_20 (.D(Input), .en(L12), .Q(Q12), .clk(in_9), .clr(in_8));
  Register #(.width(32)) register_21 (.D(Input), .en(L20), .Q(Q20), .clk(in_9), .clr(in_8));
  Register #(.width(32)) register_22 (.D(Input), .en(L28), .Q(Q28), .clk(in_9), .clr(in_8));
  Demultiplexer #(.select(5)) demultiplexer_1 (
    .out0(L0), .out1(L1), .out2(L2), .out3(L3), .out4(L4), .out5(L5), .out6(L6), .out7(L7), .out8(L8),
    .out9(L9), .out10(L10), .out11(L11), .out12(L12), .out13(L13), .out14(L14), .out15(L15), .out16(L16),
    .out17(L17), .out18(L18), .out19(L19), .out20(L20), .out21(L21), .out22(L22), .out23(L23), .out24(L24),
    .out25(L25), .out26(L26), .out27(L27), .out28(L28), .out29(L29), .out30(L30), .out31(L31), .in(in_7),
    .sel(in_4));  // open: en
  Register #(.width(32)) register_23 (.D(Input), .en(L5), .Q(Q5), .clk(in_9), .clr(in_8));
  Register #(.width(32)) register_24 (.D(Input), .en(L13), .Q(Q13), .clk(in_9), .clr(in_8));
  Register #(.width(32)) register_25 (.D(Input), .en(L21), .Q(Q21), .clk(in_9), .clr(in_8));
  Register #(.width(32)) register_26 (.D(Input), .en(L29), .Q(Q29), .clk(in_9), .clr(in_8));
  Multiplexer #(.select(5), .width(32)) multiplexer_4 (
    .in0(Q0), .in1(Q1), .in2(Q2), .in3(Q3), .in4(Q4), .in5(Q5), .in6(Q6), .in7(Q7), .in8(Q8), .in9(Q9),
    .in10(Q10), .in11(Q11), .in12(Q12), .in13(Q13), .in14(Q14), .in15(Q15), .in16(Q16), .in17(Q17),
    .in18(Q18), .in19(Q19), .in20(Q20), .in21(Q21), .in22(Q22), .in23(Q23), .in24(Q24), .in25(Q25),
    .in26(Q26), .in27(Q27), .in28(Q28), .in29(Q29), .in30(Q30), .in31(out_21), .out(Output), .sel(in_5));  // open: en
  Register #(.width(32)) register_27 (.D(Input), .en(L6), .Q(Q6), .clk(in_9), .clr(in_8));
  Register #(.width(32)) register_28 (.D(Input), .en(L14), .Q(Q14), .clk(in_9), .clr(in_8));
  Register #(.width(32)) register_29 (.D(Input), .en(L22), .Q(Q22), .clk(in_9), .clr(in_8));
  Register #(.width(32)) register_30 (.D(Input), .en(L30), .Q(Q30), .clk(in_9), .clr(in_8));
  Multiplexer #(.select(5), .width(32)) multiplexer_5 (
    .in0(Q0), .in1(Q1), .in2(Q2), .in3(Q3), .in4(Q4), .in5(Q5), .in6(Q6), .in7(Q7), .in8(Q8), .in9(Q9),
    .in10(Q10), .in11(Q11), .in12(Q12), .in13(Q13), .in14(Q14), .in15(Q15), .in16(Q16), .in17(Q17),
    .in18(Q18), .in19(Q19), .in20(Q20), .in21(Q21), .in22(Q22), .in23(Q23), .in24(Q24), .in25(Q25),
    .in26(Q26), .in27(Q27), .in28(Q28), .in29(Q29), .in30(Q30), .in31(out_21), .out(out_19), .sel(in_6));  // open: en
  Register #(.width(32)) register_31 (.D(Input), .en(L7), .Q(Q7), .clk(in_9), .clr(in_8));
  Register #(.width(32)) register_32 (.D(Input), .en(L15), .Q(Q15), .clk(in_9), .clr(in_8));
  Register #(.width(32)) register_33 (.D(Input), .en(L23), .Q(Q23), .clk(in_9), .clr(in_8));
  Multiplexer #(.width(32)) multiplexer_6 (.in0(SP), .in1(Input), .out(multiplexer_6_out), .sel(L31));  // open: en
  Register #(.width(32)) register_34 (.D(multiplexer_6_out), .en(LSP), .Q(out_21), .clk(in_9), .clr(in_8));

  // Other names for the same wires on the sheet: A[31:0] = Output; Address[4:0] = in_4; B[31:0] = out_19; CLK = in_9;
  //   DHI[31:0] = in_2; DI[31:0] = in_1; DLO[31:0] = in_3; L_HI_LO = in_11; mfhi = in_14; mflo = in_16; Pop = in_15;
  //   Push = in_13; Q31[31:0] = out_21; QHI[31:0] = out_20; QLO[31:0] = out_18; random_t = in_12; Reset = in_8;
  //   RW = in_7; Sa[4:0] = in_5; Sb[4:0] = in_6
endmodule

module Program_Counter (
  input  [31:0] PC_IN,
  input  in_2,
  input  in_3,
  input  in_4,
  output [31:0] PC_OUT
);

  Register #(.width(32)) register_1 (.D(PC_IN), .en(in_4), .Q(PC_OUT), .clk(in_2), .clr(in_3));

  // Other names for the same wires on the sheet: CLk = in_2; EN = in_4; Reset = in_3
endmodule

module Instruction_Decoder (
  input  [31:0] Instruction,
  input  in_2,
  input  in_3,
  input  in_4,
  output [5:0] Op_Code,
  output [5:0] Func_Code,
  output [4:0] Rs,
  output [4:0] Rt,
  output [4:0] Rd,
  output [15:0] out_10,
  output [25:0] out_11
);

  Register #(.width(32)) register_1 (
    .D(Instruction), .en(in_4), .Q({Op_Code, out_11[25:16], out_10[15:6], Func_Code}), .clk(in_2), .clr(in_3));

  assign out_10[5:0] = Func_Code;
  assign out_11[15:0] = {out_10[15:6], Func_Code};
  assign Rd = out_10[15:11];
  assign Rs = out_11[25:21];
  assign Rt = out_11[20:16];

  // Other names for the same wires on the sheet: Constante_Offset[15:0] = {out_10[15:6], Func_Code};
  //   Destino_Salto[25:0] = {out_11[25:16], out_10[15:6], Func_Code}; CLk = in_2; EN = in_4; Reset = in_3
endmodule

module Branch_Control (
  input  [31:0] PC,
  input  [31:0] Rs,
  input  [31:0] Rt,
  input  [15:0] Offset,
  input  [25:0] Destino,
  input  [5:0] Func_Code,
  input  [5:0] Op_Code,
  output [31:0] Next_Inst_Address
);

  wire and_1_out, and_2_out, and_3_out, and_4_out, and_5_out, beq, bgtz, blez, bltz, bne, Comp,
       comparator_1_eq, comparator_2_gt, comparator_2_lt, j, jr;
  wire [31:0] adder_1_out, adder_2_out, multiplexer_1_out, multiplexer_2_out;
  wire [31:17] PC_Offset;

  Jump_Control jump_control_1 (
    .Func_Code(Func_Code), .Op_Code(Op_Code), .jr(jr), .bltz(bltz), .j(j), .beq(beq), .bne(bne), .blez(blez),
    .bgtz(bgtz));
  assign PC_Offset = {{14{Offset[15]}}, Offset[15]};  // Bit_Extender bit_extender_1
  Adder #(.width(32)) adder_1 (.a(PC), .b(32'h4), .out(adder_1_out));  // open: cin, cout
  Multiplexer #(.width(32)) multiplexer_1 (
    .in0({32{1'b0}}), .in1({PC_Offset, Offset[14:0], 2'b00}), .out(multiplexer_1_out), .sel(Comp));  // open: en
  Adder #(.width(32)) adder_2 (.a(adder_1_out), .b(multiplexer_1_out), .out(adder_2_out));  // open: cin, cout
  Multiplexer #(.width(32)) multiplexer_2 (
    .in0(adder_2_out), .in1({PC[31:28], Destino, 2'b00}), .out(multiplexer_2_out), .sel(j));  // open: en
  Multiplexer #(.width(32)) multiplexer_3 (
    .in0(multiplexer_2_out), .in1(Rs), .out(Next_Inst_Address), .sel(jr));  // open: en
  Comparator #(.width(32)) comparator_1 (.a(Rs), .b(Rt), .eq(comparator_1_eq));  // open: gt, lt
  Comparator #(.width(32)) comparator_2 (
    .a(Rs), .b({32{1'b0}}), .gt(comparator_2_gt), .lt(comparator_2_lt));  // open: eq
  and and_1 (and_1_out, beq, comparator_1_eq);
  and and_2 (and_2_out, ~comparator_1_eq, bne);  // AND_Gate
  and and_3 (and_3_out, ~comparator_2_gt, blez);  // AND_Gate
  and and_4 (and_4_out, comparator_2_gt, bgtz);
  and and_5 (and_5_out, comparator_2_lt, bltz);
  or or_1 (Comp, and_1_out, and_2_out, and_3_out, and_4_out, and_5_out);

  // Other names for the same wires on the sheet: PC_Offset[16:2] = Offset[14:0]; PC_Out[31:0] = Next_Inst_Address;
  //   Destino_Salto[25:0] = Destino; PC_Salto[31:2] = {PC[31:28], Destino}
endmodule

module Jump_Control (
  input  [5:0] Func_Code,
  input  [5:0] Op_Code,
  output jr,
  output bltz,
  output j,
  output beq,
  output bne,
  output blez,
  output bgtz
);

  wire comparator_1_eq, comparator_2_eq;

  Comparator #(.width(6)) comparator_1 (.a(Op_Code), .b({6{1'b0}}), .eq(comparator_1_eq));  // open: gt, lt
  Comparator #(.width(6)) comparator_2 (.a(Func_Code), .b(6'b001000), .eq(comparator_2_eq));  // open: gt, lt
  Comparator #(.width(6)) comparator_3 (.a(Op_Code), .b(6'b000001), .eq(bltz));  // open: gt, lt
  Comparator #(.width(6)) comparator_4 (.a(Op_Code), .b(6'b000010), .eq(j));  // open: gt, lt
  Comparator #(.width(6)) comparator_5 (.a(Op_Code), .b(6'b000100), .eq(beq));  // open: gt, lt
  Comparator #(.width(6)) comparator_6 (.a(Op_Code), .b(6'b000101), .eq(bne));  // open: gt, lt
  Comparator #(.width(6)) comparator_7 (.a(Op_Code), .b(6'b000110), .eq(blez));  // open: gt, lt
  Comparator #(.width(6)) comparator_8 (.a(Op_Code), .b(6'b000111), .eq(bgtz));  // open: gt, lt
  and and_1 (jr, comparator_1_eq, comparator_2_eq);
endmodule

module Data_Path (
  input  [31:0] Instruccion,
  input  [31:0] KBD,
  input  CLK,
  input  Res,
  input  ID_EN,
  input  PC_EN,
  input  R_W,
  input  Start,
  input  KBD_EN,
  input  SPEN,
  output [31:0] MemoryAddres,
  output [31:0] Data_Ram,
  output [6:0] TTY,
  output [5:0] Op_Code,
  output [5:0] F_Code
);

  wire halt, I, J, kbd_en_t, L_HI_LO, lw, mfhi, mflo, or_1_out, other_operations_control_1_halt,
       other_operations_control_1_kbd, other_operations_control_1_lw, other_operations_control_1_mfhi,
       other_operations_control_1_mflo, other_operations_control_1_pop, other_operations_control_1_push,
       other_operations_control_1_rnd, other_operations_control_1_sw, other_operations_control_1_tty, pop,
       push, R, \rand , sw, tty_t;
  wire [4:0] multiplexer_3_out, Rd, Rs, Rt;
  wire [15:0] Constante_Offset;
  wire [25:0] Destino;
  wire [31:0] A, B, F, HI, LO, multiplexer_1_out, multiplexer_2_out, PC, PC_prime, QHI, QLO, SP;

  Instruction_Decoder instruction_decoder_1 (
    .Instruction(Instruccion), .in_2(CLK), .in_3(Res), .in_4(ID_EN), .Op_Code(Op_Code), .Func_Code(F_Code),
    .Rs(Rs), .Rt(Rt), .Rd(Rd), .out_10(Constante_Offset), .out_11(Destino));
  Operation_Identifier operation_identifier_1 (.Op_Code(Op_Code), .J(J), .R(R), .I(I));
  Program_Counter program_counter_1 (.PC_IN(PC_prime), .in_2(CLK), .in_3(Res), .in_4(PC_EN), .PC_OUT(PC));
  or or_1 (or_1_out, lw, pop);
  Branch_Control branch_control_1 (
    .PC(PC), .Rs(A), .Rt(B), .Offset(Constante_Offset), .Destino(Destino), .Func_Code(F_Code),
    .Op_Code(Op_Code), .Next_Inst_Address(PC_prime));
  Multiplexer #(.width(32)) multiplexer_1 (
    .in0(F), .in1(Instruccion), .out(multiplexer_1_out), .sel(or_1_out));  // open: en
  Multiplexer #(.width(32)) multiplexer_2 (
    .in0(multiplexer_1_out), .in1(KBD), .out(multiplexer_2_out), .sel(KBD_EN));  // open: en
  Multiplexer #(.width(5)) multiplexer_3 (.in0(Rd), .in1(Rt), .out(multiplexer_3_out), .sel(I));  // open: en
  Other_Operations_Control other_operations_control_1 (
    .Op_Code(Op_Code), .Func_Code(F_Code), .mfhi(other_operations_control_1_mfhi),
    .mflo(other_operations_control_1_mflo), .pop(other_operations_control_1_pop),
    .push(other_operations_control_1_push), .lw(other_operations_control_1_lw),
    .sw(other_operations_control_1_sw), .tty(other_operations_control_1_tty),
    .rnd(other_operations_control_1_rnd), .kbd(other_operations_control_1_kbd),
    .halt(other_operations_control_1_halt));
  and and_1 (mfhi, Start, other_operations_control_1_mfhi);
  and and_2 (mflo, Start, other_operations_control_1_mflo);
  and and_3 (pop, Start, other_operations_control_1_pop);
  and and_4 (push, Start, other_operations_control_1_push);
  and and_5 (lw, Start, other_operations_control_1_lw);
  and and_6 (sw, Start, other_operations_control_1_sw);
  and and_7 (tty_t, Start, other_operations_control_1_tty);
  and and_8 (\rand , Start, other_operations_control_1_rnd);
  and and_9 (kbd_en_t, Start, other_operations_control_1_kbd);
  and and_10 (halt, Start, other_operations_control_1_halt);
  Register_File register_file_1 (
    .Output(A), .out_18(QLO), .out_19(B), .out_20(QHI), .in_1(multiplexer_2_out), .in_2(HI), .in_3(LO),
    .in_4(multiplexer_3_out), .in_5(Rs), .in_6(Rt), .in_7(R_W), .in_8(Res), .in_9(CLK), .in_11(L_HI_LO),
    .in_13(push), .in_15(pop), .in_14(mfhi), .in_16(mflo), .in_12(\rand ), .out_21(SP), .SPEN(SPEN));
  Memory_Address memory_address_1 (
    .PC(PC), .SP(SP), .F(F), .push(push), .pop(pop), .lw(lw), .sw(sw), .Memory_Addres(MemoryAddres));
  Multiplexer #(.width(32)) multiplexer_4 (
    .in0(A), .in1(B), .out({Data_Ram[7:0], Data_Ram[15:8], Data_Ram[23:16], Data_Ram[31:24]}), .sel(sw));  // open: en
  ALU_2 alu_1 (
    .in_1(A), .in_2(B), .Func_Code(F_Code), .Op_Code(Op_Code), .Constante(Constante_Offset),
    .Tipo_de_Instruccion(I), .Output(F), .Hi(HI), .LO(LO), .L_HI_LO(L_HI_LO));
  Bit_Extender #(.in_width(32), .out_width(7)) bit_extender_1 (.in(A), .out(TTY));

  // Other names for the same wires on the sheet: Inst[31:0] = Instruccion
endmodule

module Operation_Identifier (
  input  [5:0] Op_Code,
  output J,
  output R,
  output I
);

  wire comparator_2_eq, comparator_3_eq, comparator_4_eq;

  Comparator #(.width(6)) comparator_1 (.a(Op_Code), .b(6'b000010), .eq(J));  // open: gt, lt
  Comparator #(.width(6)) comparator_2 (.a(Op_Code), .b({6{1'b0}}), .eq(comparator_2_eq));  // open: gt, lt
  Comparator #(.width(6)) comparator_3 (.a(Op_Code), .b(6'b111000), .eq(comparator_3_eq));  // open: gt, lt
  Comparator #(.width(6)) comparator_4 (.a(Op_Code), .b({6{1'b1}}), .eq(comparator_4_eq));  // open: gt, lt
  and and_1 (I, ~R, ~J);  // AND_Gate
  or or_1 (R, comparator_2_eq, comparator_3_eq, comparator_4_eq);
endmodule

module Other_Operations_Control (
  input  [5:0] Op_Code,
  input  [5:0] Func_Code,
  output mfhi,
  output mflo,
  output pop,
  output push,
  output lw,
  output sw,
  output tty,
  output rnd,
  output kbd,
  output halt
);

  wire comparator_1_eq, comparator_2_eq, comparator_3_eq, comparator_4_eq, comparator_5_eq, comparator_6_eq,
       comparator_9_eq, comparator_10_eq, comparator_11_eq, comparator_12_eq, comparator_13_eq;

  Comparator #(.width(6)) comparator_1 (.a(Op_Code), .b({6{1'b0}}), .eq(comparator_1_eq));  // open: gt, lt
  Comparator #(.width(6)) comparator_2 (.a(Func_Code), .b(6'b010000), .eq(comparator_2_eq));  // open: gt, lt
  Comparator #(.width(6)) comparator_3 (.a(Func_Code), .b(6'b010010), .eq(comparator_3_eq));  // open: gt, lt
  Comparator #(.width(6)) comparator_4 (.a(Op_Code), .b(6'b111000), .eq(comparator_4_eq));  // open: gt, lt
  Comparator #(.width(6)) comparator_5 (.a(Func_Code), .b({6{1'b0}}), .eq(comparator_5_eq));  // open: gt, lt
  Comparator #(.width(6)) comparator_6 (.a(Func_Code), .b(6'b000001), .eq(comparator_6_eq));  // open: gt, lt
  Comparator #(.width(6)) comparator_7 (.a(Op_Code), .b(6'b100011), .eq(lw));  // open: gt, lt
  Comparator #(.width(6)) comparator_8 (.a(Op_Code), .b(6'b101011), .eq(sw));  // open: gt, lt
  Comparator #(.width(6)) comparator_9 (.a(Op_Code), .b({6{1'b1}}), .eq(comparator_9_eq));  // open: gt, lt
  Comparator #(.width(6)) comparator_10 (.a(Func_Code), .b(6'b000001), .eq(comparator_10_eq));  // open: gt, lt
  Comparator #(.width(6)) comparator_11 (.a(Func_Code), .b(6'b000010), .eq(comparator_11_eq));  // open: gt, lt
  Comparator #(.width(6)) comparator_12 (.a(Func_Code), .b(6'b000100), .eq(comparator_12_eq));  // open: gt, lt
  Comparator #(.width(6)) comparator_13 (.a(Func_Code), .b({6{1'b1}}), .eq(comparator_13_eq));  // open: gt, lt
  and and_1 (mfhi, comparator_1_eq, comparator_2_eq);
  and and_2 (mflo, comparator_1_eq, comparator_3_eq);
  and and_3 (pop, comparator_4_eq, comparator_5_eq);
  and and_4 (push, comparator_4_eq, comparator_6_eq);
  and and_5 (tty, comparator_9_eq, comparator_10_eq);
  and and_6 (rnd, comparator_9_eq, comparator_11_eq);
  and and_7 (kbd, comparator_9_eq, comparator_12_eq);
  and and_8 (halt, comparator_9_eq, comparator_13_eq);
endmodule

module Memory_Address (
  input  [31:0] PC,
  input  [31:0] SP,
  input  [31:0] F,
  input  push,
  input  pop,
  input  lw,
  input  sw,
  output [31:0] Memory_Addres
);

  wire or_1_out, or_2_out;
  wire [31:0] multiplexer_1_out;

  Multiplexer #(.width(32)) multiplexer_1 (.in0(PC), .in1(SP), .out(multiplexer_1_out), .sel(or_1_out));  // open: en
  or or_1 (or_1_out, push, pop);
  or or_2 (or_2_out, lw, sw);
  Multiplexer #(.width(32)) multiplexer_2 (
    .in0(multiplexer_1_out), .in1(F), .out(Memory_Addres), .sel(or_2_out));  // open: en
endmodule

module Delay (
  input  [3:0] Time,
  input  Start,
  input  CLK,
  input  RES,
  output Ready
);

  wire [3:0] counter_1_q;

  Counter #(.width(4), .max('hf)) counter_1 (
    .count(Start), .Q(counter_1_q), .clk(CLK), .clr(RES));  // open: load, D, carry
  Comparator #(.width(4)) comparator_1 (.a(counter_1_q), .b(Time), .eq(Ready));  // open: gt, lt
endmodule

module Reading (
  input  [3:0] Time,
  input  [31:0] Ram_00,
  input  [31:0] Ram_01,
  input  [31:0] Ram_10,
  input  [31:0] Ram_11,
  input  Read,
  input  CLK,
  input  RES,
  output [31:0] Ram_00_2,
  output [31:0] Ram_01_2,
  output [31:0] Ram_10_2,
  output [31:0] Ram_11_2,
  output CS,
  output Ready
);

  wire delay_1_ready, EN, or_1_out, Start;

  or or_1 (or_1_out, Read, delay_1_ready);
  D_Flip_Flop #(.trigger("falling")) d_ff_1 (.clk(CLK), .D(Read), .Q(Start), .en(or_1_out));  // open: Qn, preset, reset
  Delay delay_1 (.Time(Time), .Start(Start), .CLK(CLK), .RES(Ready), .Ready(delay_1_ready));
  D_Flip_Flop #(.trigger("falling")) d_ff_2 (
    .clk(CLK), .D(delay_1_ready), .Q(EN), .reset(Ready));  // open: Qn, preset, en
  D_Flip_Flop #(.trigger("falling")) d_ff_3 (.clk(CLK), .D(EN), .Q(Ready));  // open: Qn, preset, en, reset
  Register #(.width(32)) register_1 (.D(Ram_00), .en(EN), .Q(Ram_00_2), .clk(CLK), .clr(RES));
  Register #(.width(32)) register_2 (.D(Ram_01), .en(EN), .Q(Ram_01_2), .clk(CLK), .clr(RES));
  Register #(.width(32)) register_3 (.D(Ram_10), .en(EN), .Q(Ram_10_2), .clk(CLK), .clr(RES));
  Register #(.width(32)) register_4 (.D(Ram_11), .en(EN), .Q(Ram_11_2), .clk(CLK), .clr(RES));
  or or_2 (CS, Start, EN);

  // Other names for the same wires on the sheet: _00[31:0] = Ram_00; _01[31:0] = Ram_01; _10[31:0] = Ram_10;
  //   _11[31:0] = Ram_11
endmodule

module Access (
  input  [31:0] Address,
  input  [31:0] Ram_00,
  input  [31:0] Ram_01,
  input  [31:0] Ram_10,
  input  [31:0] Ram_11,
  input  [3:0] Read_Time,
  input  [3:0] Write_Time,
  input  Read,
  input  CLK,
  input  RES,
  input  Read_Inst,
  input  Read_Data,
  input  Load,
  output [3:0] Mask,
  output [15:0] Address_2,
  output [31:0] RAM_OUT,
  output RW,
  output Chip_Select,
  output Ready_Inst,
  output Ready_Data,
  output Ready_write
);

  wire CS_Data, CS_Inst, delay_1_ready, EN, or_1_out;
  wire [31:0] _00_Out, _01_Out, _10_Out, _11_Out, D0_Out, D1_Out, D2_Out, D3_Out, I0_Out, I1_Out, I2_Out,
       I3_Out;

  Multiplexer #(.width(32)) multiplexer_1 (.in0(D0_Out), .in1(I0_Out), .out(_00_Out), .sel(Load));  // open: en
  D_Flip_Flop #(.trigger("falling")) d_ff_1 (.clk(CLK), .D(Read), .Q(RW), .en(or_1_out));  // open: Qn, preset, reset
  or or_1 (or_1_out, Read, delay_1_ready);
  Delay delay_1 (.Time(Write_Time), .Start(RW), .CLK(CLK), .RES(Ready_write), .Ready(delay_1_ready));
  Reading reading_1 (
    .Time(Read_Time), .Ram_00(Ram_00), .Ram_01(Ram_01), .Ram_10(Ram_10), .Ram_11(Ram_11), .Read(Read_Inst),
    .CLK(CLK), .RES(RES), .Ram_00_2(I0_Out), .Ram_01_2(I1_Out), .Ram_10_2(I2_Out), .Ram_11_2(I3_Out),
    .CS(CS_Inst), .Ready(Ready_Inst));
  Multiplexer #(.width(32)) multiplexer_2 (.in0(D1_Out), .in1(I1_Out), .out(_01_Out), .sel(Load));  // open: en
  D_Flip_Flop #(.trigger("falling")) d_ff_2 (
    .clk(CLK), .D(delay_1_ready), .Q(EN), .reset(Ready_write));  // open: Qn, preset, en
  Multiplexer #(.width(32)) multiplexer_3 (.in0(D2_Out), .in1(I2_Out), .out(_10_Out), .sel(Load));  // open: en
  D_Flip_Flop #(.trigger("falling")) d_ff_3 (.clk(CLK), .D(EN), .Q(Ready_write));  // open: Qn, preset, en, reset
  Multiplexer #(.width(32)) multiplexer_4 (.in0(D3_Out), .in1(I3_Out), .out(_11_Out), .sel(Load));  // open: en
  Decoder #(.select(2)) decoder_1 (
    .out0(Mask[0]), .out1(Mask[1]), .out2(Mask[2]), .out3(Mask[3]), .sel(Address[3:2]));  // open: en
  Reading reading_2 (
    .Time(Read_Time), .Ram_00(Ram_00), .Ram_01(Ram_01), .Ram_10(Ram_10), .Ram_11(Ram_11), .Read(Read_Data),
    .CLK(CLK), .RES(RES), .Ram_00_2(D0_Out), .Ram_01_2(D1_Out), .Ram_10_2(D2_Out), .Ram_11_2(D3_Out),
    .CS(CS_Data), .Ready(Ready_Data));
  Multiplexer #(.select(2), .width(32)) multiplexer_5 (
    .in0(_00_Out), .in1(_01_Out), .in2(_10_Out), .in3(_11_Out),
    .out({RAM_OUT[7:0], RAM_OUT[15:8], RAM_OUT[23:16], RAM_OUT[31:24]}), .sel(Address[3:2]));  // open: en
  or or_2 (Chip_Select, RW, CS_Inst, CS_Data);

  assign Address_2 = Address[19:4];

  // Other names for the same wires on the sheet: _00[31:0] = Ram_00; _01[31:0] = Ram_01; _10[31:0] = Ram_10;
  //   _11[31:0] = Ram_11; DP_Address[31:0] = Address; Mask_t[1:0] = Address[3:2]; Adress[15:0] = Address[19:4];
  //   Ready_W = Ready_write; RW_t = Read; Start = RW
endmodule

module Control_Unit (
  input  in_1,
  input  in_2,
  input  in_3,
  input  in_4,
  input  in_5,
  input  in_6,
  input  [5:0] in_7,
  input  [5:0] in_8,
  output Get_Inst,
  output PCen,
  output SPen,
  output INSTen,
  output KBDen,
  output RegW,
  output TTYen,
  output WriteD,
  output startEN,
  output Get_Data,
  output End
);

  wire ALU, and_1_out, and_2_out, and_3_out, and_5_out, Copy, d_ff_1_q, d_ff_4_q, d_ff_6_q, d_ff_8_q,
       d_ff_9_q, demultiplexer_1_out0, demultiplexer_2_out0, demultiplexer_3_out0, demultiplexer_4_out0,
       demultiplexer_4_out1, halt, Jump, kbd, lw, Memory, or_1_out, or_3_out, or_4_out, or_5_out, pop, push,
       \rand , SP_1, SP_2, Specials, startEN_t, sw, tty;

  Demultiplexer demultiplexer_1 (
    .out0(demultiplexer_1_out0), .out1(Get_Data), .in(d_ff_1_q), .sel(or_1_out));  // open: en
  D_Flip_Flop #(.trigger("falling")) d_ff_1 (
    .clk(in_2), .D(Memory), .Q(d_ff_1_q), .reset(in_3));  // open: Qn, preset, en
  D_Flip_Flop #(.trigger("falling")) d_ff_2 (
    .clk(in_2), .D(in_4), .Q(startEN_t), .reset(in_3));  // open: Qn, preset, en
  or or_1 (or_1_out, lw, pop);
  Demultiplexer demultiplexer_2 (
    .out0(demultiplexer_2_out0), .out1(SP_1), .in(demultiplexer_1_out0), .sel(push));  // open: en
  D_Flip_Flop #(.trigger("falling")) d_ff_3 (
    .clk(in_2), .Q(startEN), .preset(startEN_t), .reset(PCen));  // open: D, Qn, en
  D_Flip_Flop #(.trigger("falling")) d_ff_4 (.clk(in_2), .D(SP_1), .Q(d_ff_4_q), .reset(in_3));  // open: Qn, preset, en
  Operations operations_1 (
    .Func_Code(in_8), .Op_Code(in_7), .EN(startEN_t), .ALU(ALU), .Copy(Copy), .Jump(Jump), .Memory(Memory),
    .Specials(Specials));
  and and_1 (and_1_out, Specials, \rand );
  and and_2 (and_2_out, Specials, kbd);
  or or_2 (WriteD, demultiplexer_2_out0, d_ff_4_q);
  Other_Operations_Control other_operations_control_1 (
    .Op_Code(in_7), .Func_Code(in_8), .pop(pop), .push(push), .lw(lw), .sw(sw), .tty(tty), .rnd(\rand ),
    .kbd(kbd), .halt(halt));  // open: mfhi, mflo
  or or_3 (or_3_out, ALU, Copy, and_1_out, and_2_out, in_5);
  D_Flip_Flop #(.trigger("falling")) d_ff_5 (.clk(in_2), .D(or_3_out), .Q(RegW));  // open: Qn, preset, en, reset
  or or_4 (or_4_out, End, and_3_out);
  and and_3 (and_3_out, Specials, halt);
  D_Flip_Flop #(.trigger("falling")) d_ff_6 (.clk(in_2), .D(RegW), .Q(d_ff_6_q), .reset(in_3));  // open: Qn, preset, en
  D_Flip_Flop #(.trigger("falling")) d_ff_7 (.clk(in_2), .D(or_4_out), .Q(End), .reset(in_3));  // open: Qn, preset, en
  Demultiplexer demultiplexer_3 (.out0(demultiplexer_3_out0), .out1(SP_2), .in(d_ff_6_q), .sel(pop));  // open: en
  and and_4 (KBDen, kbd, demultiplexer_3_out0);
  D_Flip_Flop #(.trigger("falling")) d_ff_8 (.clk(in_2), .D(SP_2), .Q(d_ff_8_q), .reset(in_3));  // open: Qn, preset, en
  and and_5 (and_5_out, Specials, tty);
  D_Flip_Flop #(.trigger("falling")) d_ff_9 (
    .clk(in_2), .D(demultiplexer_4_out0), .Q(d_ff_9_q), .preset(in_3));  // open: Qn, en, reset
  Demultiplexer demultiplexer_4 (
    .out0(demultiplexer_4_out0), .out1(demultiplexer_4_out1), .in(d_ff_9_q), .sel(in_1));  // open: en
  or or_5 (or_5_out, demultiplexer_3_out0, in_6, Jump, and_5_out, d_ff_8_q);
  or or_6 (Get_Inst, demultiplexer_4_out1, PCen);
  D_Flip_Flop #(.trigger("falling")) IDLE (.clk(in_2), .D(or_5_out), .Q(PCen), .reset(in_3));  // open: Qn, preset, en
  or or_7 (SPen, SP_1, SP_2);
  and and_6 (TTYen, Specials, tty, startEN);

  assign INSTen = in_4;

  // Other names for the same wires on the sheet: CLK = in_2; En = startEN; F_Code[5:0] = in_8; kbd_EN = KBDen;
  //   Op_code[5:0] = in_7; Ready_Data = in_5; Inst_EN = in_4; Ready_Inst = in_4; Ready_Write = in_6; RegEN = RegW;
  //   Res = in_3; START = in_1; stopEN = PCen; Write_Data = WriteD
endmodule

module Operations (
  input  [5:0] Func_Code,
  input  [5:0] Op_Code,
  input  EN,
  output ALU,
  output Copy,
  output Jump,
  output Memory,
  output Specials
);

  wire ALU_t, and_1_out, and_2_out, and_3_out, and_4_out, and_5_out, comparator_1_eq, comparator_2_eq,
       comparator_3_eq, comparator_4_eq, comparator_5_eq, comparator_6_eq, comparator_7_lt, comparator_8_eq,
       comparator_9_eq, comparator_10_eq, Copy_t, I, J, Jump_t, Memory_t, R, Specials_t;

  Operation_Identifier operation_identifier_1 (.Op_Code(Op_Code), .J(J), .R(R), .I(I));
  Comparator #(.width(6), .mode("unsigned")) comparator_1 (
    .a(Op_Code), .b({6{1'b0}}), .eq(comparator_1_eq));  // open: gt, lt
  Comparator #(.width(6), .mode("unsigned")) comparator_2 (
    .a(Func_Code), .b(6'b010010), .eq(comparator_2_eq));  // open: gt, lt
  Comparator #(.width(6), .mode("unsigned")) comparator_3 (
    .a(Func_Code), .b(6'b010000), .eq(comparator_3_eq));  // open: gt, lt
  Comparator #(.width(6), .mode("unsigned")) comparator_4 (
    .a(Op_Code), .b({6{1'b0}}), .eq(comparator_4_eq));  // open: gt, lt
  and and_1 (and_1_out, comparator_4_eq, comparator_5_eq);
  Comparator #(.width(6), .mode("unsigned")) comparator_5 (
    .a(Func_Code), .b({6{1'b0}}), .eq(comparator_5_eq));  // open: gt, lt
  Comparator #(.width(6), .mode("unsigned")) comparator_6 (
    .a(Func_Code), .b(6'b001000), .eq(comparator_6_eq));  // open: gt, lt
  Comparator #(.width(6), .mode("unsigned")) comparator_7 (
    .a(Op_Code), .b(6'b001000), .lt(comparator_7_lt));  // open: gt, eq
  Comparator #(.width(6), .mode("unsigned")) comparator_8 (
    .a(Op_Code), .b(6'b111000), .eq(comparator_8_eq));  // open: gt, lt
  Comparator #(.width(6), .mode("unsigned")) comparator_9 (
    .a(Op_Code), .b(6'b100011), .eq(comparator_9_eq));  // open: gt, lt
  Comparator #(.width(6), .mode("unsigned")) comparator_10 (
    .a(Op_Code), .b(6'b101011), .eq(comparator_10_eq));  // open: gt, lt
  Comparator #(.width(6), .mode("unsigned")) comparator_11 (
    .a(Op_Code), .b({6{1'b1}}), .eq(Specials_t));  // open: gt, lt
  and and_2 (and_2_out, comparator_1_eq, comparator_2_eq);
  or or_1 (Copy_t, and_2_out, and_3_out);
  and and_3 (and_3_out, comparator_1_eq, comparator_3_eq);
  and and_4 (and_4_out, comparator_4_eq, comparator_6_eq);
  and and_5 (and_5_out, I, comparator_7_lt);
  or or_2 (Memory_t, comparator_8_eq, comparator_9_eq, comparator_10_eq);
  or or_3 (Jump_t, and_1_out, and_4_out, and_5_out);
  nor nor_1 (ALU_t, Copy_t, Jump_t, Memory_t, Specials_t);
  and and_6 (ALU, EN, ALU_t);
  and and_7 (Copy, EN, Copy_t);
  and and_8 (Jump, EN, Jump_t);
  and and_9 (Memory, EN, Memory_t);
  and and_10 (Specials, EN, Specials_t);
endmodule
